# Fritzing sketch Untitled Sketch (saved by Fritzing 0.9.4)
breadboards: 1

parts:
  Parça1 = Arduino Uno (Rev3)
  TP1 = TP4056 [chip_label=TP4056 package="DIP (Dual Inline) [THT]"]
  Parça2 = Adafruit Analog 2-Axis Joystick [part_number="Adafruit #512"]
  SERVO1 = Tower Pro SG90 servo [part_number=101246]
  SERVO2 = Tower Pro SG90 servo [part_number=101246]
  SERVO3 = Tower Pro SG90 servo [part_number=101246]
  SERVO4 = Tower Pro SG90 servo [part_number=101246]
  J1 = Piezo Speaker
  S1 = SWITCH-MOMENTARY-2 [package=tactile-pth-12mm]
  S2 = SWITCH-MOMENTARY-2 [package=tactile-pth-12mm]  # not connected

nets:
  N1: Parça1.A0, Parça2.XOUT
  N2: Parça1.A1, Parça2.YOUT
  N3: Parça1.D9_PWM, SERVO3.Signal
  N4: Parça1.D10_PWM/SS, SERVO2.Signal
  N5: Parça1.D11_PWM/MOSI, SERVO1.Signal
  N6: Parça1.D2, Parça2.SWITCH
  N7: Parça1.D3_PWM, SERVO4.Signal
  N8: Parça1.D4, S1.2
  N9: Parça1.D6_PWM, J1.pin2
  +5V: TP1.pin3, Parça2.VCC, SERVO1.+5V, SERVO2.+5V, SERVO3.+5V, SERVO4.+5V
  GND: TP1.pin6, Parça2.GND, SERVO1.GND, SERVO2.GND, SERVO3.GND, SERVO4.GND, S1.1

custom parts:
  TP4056: A DIP stand-in part for whatever IC you want. With 6 pins on a 300mil dual inline package (DIP) footprint.
  Adafruit Analog 2-Axis Joystick: This mini-kit makes it easy to mount a PSP/Xbox-like thumb joystick to your project. The thumbstick is an analog joystick - more accurate and sensitive than just 'directional' joysticks - with a 'press in to select' button. Since it's analog, you'll need two analog reading pins on your microcontroller to determine X and Y. Having an extra digital input will let you read the switch. The pack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
  Tower Pro SG90 servo: Original file by John De Cristofaro http://www.adafruit.com/products/1449 Adafruit Feedback Servo (Small) Edited by: e-radionica.com 28/9/2015
